// Logisim project GhanaCore5_HazardUnits_gated.circ as structural Verilog: 3 circuits, main circuit Forwarding_Unit
module Forwarding_Unit (
  input  EXMEM_Rd_0,
  input  EXMEM_Rd_1,
  input  EXMEM_Rd_2,
  input  EXMEM_Rd_3,
  input  EXMEM_Rd_4,
  input  EXMEM_RegWrite,
  input  EXMEM_Rd_NZ,
  input  MEMWB_Rd_0,
  input  MEMWB_Rd_1,
  input  MEMWB_Rd_2,
  input  MEMWB_Rd_3,
  input  MEMWB_Rd_4,
  input  MEMWB_RegWrite,
  input  MEMWB_Rd_NZ,
  input  IDEX_Rs_0,
  input  IDEX_Rs_1,
  input  IDEX_Rs_2,
  input  IDEX_Rs_3,
  input  IDEX_Rs_4,
  input  IDEX_Rt_0,
  input  IDEX_Rt_1,
  input  IDEX_Rt_2,
  input  IDEX_Rt_3,
  input  IDEX_Rt_4,
  output ForwardA_bit1,
  output ForwardA_bit0,
  output ForwardB_bit1,
  output ForwardB_bit0
);

  wire and_1_out, and_2_p3, and_3_out, and_4_out, and_5_out, and_6_p3, and_7_out, and_8_out, and_9_out,
       and_10_p3, and_11_out, and_12_out, and_13_out, and_14_p3, and_15_out, and_16_out, and_17_out,
       and_18_out, and_19_out, and_20_out, and_22_out, and_24_out, not_1_out, not_2_out, xnor_1_p6,
       xnor_2_out, xnor_3_p9, xnor_4_out, xnor_5_p6, xnor_6_p6, xnor_7_out, xnor_8_p9, xnor_9_out,
       xnor_10_p6, xnor_11_p6, xnor_12_out, xnor_13_p9, xnor_14_out, xnor_15_out, xnor_16_out, xnor_17_out,
       xnor_18_out, xnor_19_out, xnor_20_out;

  // XNOR_Gate xnor_1: pin names not known; wires that end beside it: EXMEM_Rd_0, IDEX_Rs_0, EXMEM_Rd_1, IDEX_Rs_1, EXMEM_Rd_2, xnor_1_p6
  // XNOR_Gate xnor_2 has open pins: out=xnor_2_out
  // XNOR_Gate xnor_3: pin names not known; wires that end beside it: IDEX_Rs_0, EXMEM_Rd_1, IDEX_Rs_1, EXMEM_Rd_2, IDEX_Rs_2, EXMEM_Rd_3, IDEX_Rs_3, EXMEM_Rd_4, xnor_3_p9
  // XNOR_Gate xnor_4 has open pins: out=xnor_4_out
  // XNOR_Gate xnor_5: pin names not known; wires that end beside it: IDEX_Rs_2, EXMEM_Rd_3, IDEX_Rs_3, EXMEM_Rd_4, IDEX_Rs_4, xnor_5_p6
  // XNOR_Gate xnor_6: pin names not known; wires that end beside it: MEMWB_Rd_0, IDEX_Rs_0, MEMWB_Rd_1, IDEX_Rs_1, MEMWB_Rd_2, xnor_6_p6
  // XNOR_Gate xnor_7 has open pins: out=xnor_7_out
  // XNOR_Gate xnor_8: pin names not known; wires that end beside it: IDEX_Rs_0, MEMWB_Rd_1, IDEX_Rs_1, MEMWB_Rd_2, IDEX_Rs_2, MEMWB_Rd_3, IDEX_Rs_3, MEMWB_Rd_4, xnor_8_p9
  // XNOR_Gate xnor_9 has open pins: out=xnor_9_out
  // XNOR_Gate xnor_10: pin names not known; wires that end beside it: IDEX_Rs_2, MEMWB_Rd_3, IDEX_Rs_3, MEMWB_Rd_4, IDEX_Rs_4, xnor_10_p6
  // XNOR_Gate xnor_11: pin names not known; wires that end beside it: EXMEM_Rd_0, IDEX_Rt_0, EXMEM_Rd_1, IDEX_Rt_1, EXMEM_Rd_2, xnor_11_p6
  // XNOR_Gate xnor_12 has open pins: out=xnor_12_out
  // XNOR_Gate xnor_13: pin names not known; wires that end beside it: IDEX_Rt_0, EXMEM_Rd_1, IDEX_Rt_1, EXMEM_Rd_2, IDEX_Rt_2, EXMEM_Rd_3, IDEX_Rt_3, EXMEM_Rd_4, xnor_13_p9
  // XNOR_Gate xnor_14 has open pins: out=xnor_14_out
  // XNOR_Gate xnor_15 has open pins: out=xnor_15_out
  // XNOR_Gate xnor_16 has open pins: out=xnor_16_out
  // XNOR_Gate xnor_17 has open pins: out=xnor_17_out
  // XNOR_Gate xnor_18 has open pins: out=xnor_18_out
  // XNOR_Gate xnor_19 has open pins: out=xnor_19_out
  // XNOR_Gate xnor_20 has open pins: out=xnor_20_out
  // AND_Gate and_1 has open pins: out=and_1_out
  // AND_Gate and_2: pin names not known; wires that end beside it: xnor_6_p6, xnor_7_out, and_2_p3
  // AND_Gate and_3 has open pins: out=and_3_out
  // AND_Gate and_4 has open pins: out=and_4_out
  // AND_Gate and_5 has open pins: out=and_5_out
  // AND_Gate and_6: pin names not known; wires that end beside it: and_2_p3, xnor_8_p9, and_6_p3
  // AND_Gate and_7 has open pins: out=and_7_out
  // AND_Gate and_8 has open pins: out=and_8_out
  // AND_Gate and_9 has open pins: out=and_9_out
  // AND_Gate and_10: pin names not known; wires that end beside it: and_6_p3, xnor_9_out, and_10_p3
  // AND_Gate and_11 has open pins: out=and_11_out
  // AND_Gate and_12 has open pins: out=and_12_out
  // AND_Gate and_13 has open pins: out=and_13_out
  // AND_Gate and_14: pin names not known; wires that end beside it: and_10_p3, xnor_10_p6, and_14_p3
  // AND_Gate and_15 has open pins: out=and_15_out
  // AND_Gate and_16 has open pins: out=and_16_out
  // AND_Gate and_17 has open pins: out=and_17_out
  // AND_Gate and_18 has open pins: out=and_18_out
  // AND_Gate and_19 has open pins: out=and_19_out
  // AND_Gate and_20 has open pins: out=and_20_out
  // AND_Gate and_21 has open pins: out=ForwardA_bit1
  // AND_Gate and_22 has open pins: out=and_22_out
  // AND_Gate and_23 has open pins: out=ForwardB_bit1
  // AND_Gate and_24 has open pins: out=and_24_out
  not not_1 (not_1_out, ForwardA_bit1);
  not not_2 (not_2_out, ForwardB_bit1);
  // AND_Gate and_25 has open pins: out=ForwardA_bit0
  // AND_Gate and_26 has open pins: out=ForwardB_bit0
endmodule

module Hazard_Detection_Unit (
  input  IDEX_MemRead,
  input  IDEX_Rt_NZ,
  input  IFID_UsesRs,
  input  IFID_UsesRt,
  input  IDEX_Rt_0,
  input  IDEX_Rt_1,
  input  IDEX_Rt_2,
  input  IDEX_Rt_3,
  input  IDEX_Rt_4,
  input  IFID_Rs_0,
  input  IFID_Rs_1,
  input  IFID_Rs_2,
  input  IFID_Rs_3,
  input  IFID_Rs_4,
  input  IFID_Rt_0,
  input  IFID_Rt_1,
  input  IFID_Rt_2,
  input  IFID_Rt_3,
  input  IFID_Rt_4,
  output Stall
);

  wire and_1_p3, and_2_out, and_3_p3, and_4_out, and_5_p3, and_6_out, and_7_p3, and_8_out, and_9_out,
       and_10_out, and_11_out, or_1_out, xnor_1_p6, xnor_2_out, xnor_3_p9, xnor_4_out, xnor_5_p6, xnor_6_p6,
       xnor_7_out, xnor_8_p9, xnor_9_out, xnor_10_p6;

  // XNOR_Gate xnor_1: pin names not known; wires that end beside it: IDEX_Rt_0, IFID_Rs_0, IDEX_Rt_1, IFID_Rs_1, IDEX_Rt_2, xnor_1_p6
  // XNOR_Gate xnor_2 has open pins: out=xnor_2_out
  // XNOR_Gate xnor_3: pin names not known; wires that end beside it: IFID_Rs_0, IDEX_Rt_1, IFID_Rs_1, IDEX_Rt_2, IFID_Rs_2, IDEX_Rt_3, IFID_Rs_3, IDEX_Rt_4, xnor_3_p9
  // XNOR_Gate xnor_4 has open pins: out=xnor_4_out
  // XNOR_Gate xnor_5: pin names not known; wires that end beside it: IFID_Rs_2, IDEX_Rt_3, IFID_Rs_3, IDEX_Rt_4, IFID_Rs_4, xnor_5_p6
  // XNOR_Gate xnor_6: pin names not known; wires that end beside it: IDEX_Rt_0, IFID_Rt_0, IDEX_Rt_1, IFID_Rt_1, IDEX_Rt_2, xnor_6_p6
  // XNOR_Gate xnor_7 has open pins: out=xnor_7_out
  // XNOR_Gate xnor_8: pin names not known; wires that end beside it: IFID_Rt_0, IDEX_Rt_1, IFID_Rt_1, IDEX_Rt_2, IFID_Rt_2, IDEX_Rt_3, IFID_Rt_3, IDEX_Rt_4, xnor_8_p9
  // XNOR_Gate xnor_9 has open pins: out=xnor_9_out
  // XNOR_Gate xnor_10: pin names not known; wires that end beside it: IFID_Rt_2, IDEX_Rt_3, IFID_Rt_3, IDEX_Rt_4, IFID_Rt_4, xnor_10_p6
  // AND_Gate and_1: pin names not known; wires that end beside it: xnor_1_p6, xnor_2_out, and_1_p3
  // AND_Gate and_2 has open pins: out=and_2_out
  // AND_Gate and_3: pin names not known; wires that end beside it: and_1_p3, xnor_3_p9, and_3_p3
  // AND_Gate and_4 has open pins: out=and_4_out
  // AND_Gate and_5: pin names not known; wires that end beside it: and_3_p3, xnor_4_out, and_5_p3
  // AND_Gate and_6 has open pins: out=and_6_out
  // AND_Gate and_7: pin names not known; wires that end beside it: and_5_p3, xnor_5_p6, and_7_p3
  // AND_Gate and_8 has open pins: out=and_8_out
  // AND_Gate and_9 has open pins: out=and_9_out
  // AND_Gate and_10 has open pins: out=and_10_out
  // OR_Gate or_1 has open pins: out=or_1_out
  // AND_Gate and_11 has open pins: out=and_11_out
  // AND_Gate and_12 has open pins: out=Stall
endmodule

module Branch_Forward_Stall (
  input  IsBranch,
  input  IDEX_RegWrite,
  input  IDEX_Rd_NZ,
  input  EXMEM_RegWrite,
  input  EXMEM_Rd_NZ,
  input  EXMEM_MemRead,
  input  IDEX_Rd_0,
  input  IDEX_Rd_1,
  input  IDEX_Rd_2,
  input  IDEX_Rd_3,
  input  IDEX_Rd_4,
  input  EXMEM_Rd_0,
  input  EXMEM_Rd_1,
  input  EXMEM_Rd_2,
  input  EXMEM_Rd_3,
  input  EXMEM_Rd_4,
  input  IFID_Rs_0,
  input  IFID_Rs_1,
  input  IFID_Rs_2,
  input  IFID_Rs_3,
  input  IFID_Rs_4,
  input  IFID_Rt_0,
  input  IFID_Rt_1,
  input  IFID_Rt_2,
  input  IFID_Rt_3,
  input  IFID_Rt_4,
  output BranchStall,
  output ForwardC,
  output ForwardD
);

  wire and_1_p3, and_2_out, and_3_out, and_4_out, and_5_p3, and_6_out, and_7_out, and_8_out, and_9_p3,
       and_10_out, and_11_out, and_12_out, and_13_p3, and_14_out, and_15_out, and_16_out, and_17_out,
       and_18_out, and_19_out, and_20_out, and_21_out, and_22_out, and_23_out, and_24_out, and_26_out,
       and_27_out, not_1_out, or_1_p3, or_2_out, or_3_out, xnor_1_out, xnor_2_out, xnor_3_p9, xnor_4_out,
       xnor_5_p6, xnor_6_p6, xnor_7_out, xnor_8_p9, xnor_9_out, xnor_10_p6, xnor_11_p6, xnor_12_out,
       xnor_13_p9, xnor_14_out, xnor_15_p6, xnor_16_p6, xnor_17_out, xnor_18_out, xnor_19_out, xnor_20_out;

  // XNOR_Gate xnor_1 has open pins: out=xnor_1_out
  // XNOR_Gate xnor_2 has open pins: out=xnor_2_out
  // XNOR_Gate xnor_3: pin names not known; wires that end beside it: IFID_Rs_0, IDEX_Rd_1, IFID_Rs_1, IDEX_Rd_2, IFID_Rs_2, IDEX_Rd_3, IFID_Rs_3, IDEX_Rd_4, xnor_3_p9
  // XNOR_Gate xnor_4 has open pins: out=xnor_4_out
  // XNOR_Gate xnor_5: pin names not known; wires that end beside it: IFID_Rs_2, IDEX_Rd_3, IFID_Rs_3, IDEX_Rd_4, IFID_Rs_4, xnor_5_p6
  // XNOR_Gate xnor_6: pin names not known; wires that end beside it: IDEX_Rd_0, IFID_Rt_0, IDEX_Rd_1, IFID_Rt_1, IDEX_Rd_2, xnor_6_p6
  // XNOR_Gate xnor_7 has open pins: out=xnor_7_out
  // XNOR_Gate xnor_8: pin names not known; wires that end beside it: IFID_Rt_0, IDEX_Rd_1, IFID_Rt_1, IDEX_Rd_2, IFID_Rt_2, IDEX_Rd_3, IFID_Rt_3, IDEX_Rd_4, xnor_8_p9
  // XNOR_Gate xnor_9 has open pins: out=xnor_9_out
  // XNOR_Gate xnor_10: pin names not known; wires that end beside it: IFID_Rt_2, IDEX_Rd_3, IFID_Rt_3, IDEX_Rd_4, IFID_Rt_4, xnor_10_p6
  // XNOR_Gate xnor_11: pin names not known; wires that end beside it: EXMEM_Rd_0, IFID_Rs_0, EXMEM_Rd_1, IFID_Rs_1, EXMEM_Rd_2, xnor_11_p6
  // XNOR_Gate xnor_12 has open pins: out=xnor_12_out
  // XNOR_Gate xnor_13: pin names not known; wires that end beside it: IFID_Rs_0, EXMEM_Rd_1, IFID_Rs_1, EXMEM_Rd_2, IFID_Rs_2, EXMEM_Rd_3, IFID_Rs_3, EXMEM_Rd_4, xnor_13_p9
  // XNOR_Gate xnor_14 has open pins: out=xnor_14_out
  // XNOR_Gate xnor_15: pin names not known; wires that end beside it: IFID_Rs_2, EXMEM_Rd_3, IFID_Rs_3, EXMEM_Rd_4, IFID_Rs_4, xnor_15_p6
  // XNOR_Gate xnor_16: pin names not known; wires that end beside it: EXMEM_Rd_0, IFID_Rt_0, EXMEM_Rd_1, IFID_Rt_1, EXMEM_Rd_2, xnor_16_p6
  // XNOR_Gate xnor_17 has open pins: out=xnor_17_out
  // XNOR_Gate xnor_18 has open pins: out=xnor_18_out
  // XNOR_Gate xnor_19 has open pins: out=xnor_19_out
  // XNOR_Gate xnor_20 has open pins: out=xnor_20_out
  // AND_Gate and_1: pin names not known; wires that end beside it: xnor_1_out, xnor_2_out, and_1_p3
  // AND_Gate and_2 has open pins: out=and_2_out
  // AND_Gate and_3 has open pins: out=and_3_out
  // AND_Gate and_4 has open pins: out=and_4_out
  // AND_Gate and_5: pin names not known; wires that end beside it: and_1_p3, xnor_3_p9, and_5_p3
  // AND_Gate and_6 has open pins: out=and_6_out
  // AND_Gate and_7 has open pins: out=and_7_out
  // AND_Gate and_8 has open pins: out=and_8_out
  // AND_Gate and_9: pin names not known; wires that end beside it: and_5_p3, xnor_4_out, and_9_p3
  // AND_Gate and_10 has open pins: out=and_10_out
  // AND_Gate and_11 has open pins: out=and_11_out
  // AND_Gate and_12 has open pins: out=and_12_out
  // AND_Gate and_13: pin names not known; wires that end beside it: and_9_p3, xnor_5_p6, and_13_p3
  // AND_Gate and_14 has open pins: out=and_14_out
  // AND_Gate and_15 has open pins: out=and_15_out
  // AND_Gate and_16 has open pins: out=and_16_out
  // OR_Gate or_1: pin names not known; wires that end beside it: and_13_p3, and_14_out, or_1_p3
  // OR_Gate or_2 has open pins: out=or_2_out
  // AND_Gate and_17 has open pins: out=and_17_out
  // AND_Gate and_18 has open pins: out=and_18_out
  // AND_Gate and_19 has open pins: out=and_19_out
  // AND_Gate and_20 has open pins: out=and_20_out
  // AND_Gate and_21 has open pins: out=and_21_out
  // AND_Gate and_22 has open pins: out=and_22_out
  // AND_Gate and_23 has open pins: out=and_23_out
  // AND_Gate and_24 has open pins: out=and_24_out
  // OR_Gate or_3 has open pins: out=or_3_out
  // AND_Gate and_25 has open pins: out=BranchStall
  not not_1 (not_1_out, BranchStall);
  // AND_Gate and_26 has open pins: out=and_26_out
  // AND_Gate and_27 has open pins: out=and_27_out
  // AND_Gate and_28 has open pins: out=ForwardC
  // AND_Gate and_29 has open pins: out=ForwardD
endmodule
