// Logisim project hazard_pipeline.circ as structural Verilog: 1 circuit, main circuit hazard_pipeline
module hazard_pipeline (
  input  RESET,
  output [31:0] PC,
  output [31:0] ALU_EX,
  output RegWrite_WB,
  output [4:0] WriteReg,
  output [31:0] WriteData
);

  Clock CLK ();  // open: out
  Register #(.width(32)) register_1 ();  // open: D, en, clk, Q, clr
  Register #(.width(32)) IF_ID ();  // open: D, en, clk, Q, clr
  Register #(.width(32)) ID_EX ();  // open: D, en, clk, Q, clr
  Register #(.width(32)) EX_MEM ();  // open: D, en, clk, Q, clr
  Register #(.width(32)) MEM_WB ();  // open: D, en, clk, Q, clr
endmodule
